# Fritzing sketch CompletedBoard (saved by Fritzing 0.9.4)
breadboards: 1

parts:
  U1 = ESP32S-HiLetgo [part_number=ESP32S-HiLetgo]
  DHT1 = DHT11 Humitidy and Temperature Sensor
  R1 = Resistor [tolerance=±5% resistance=4.7k package="1206 [SMD]"]

nets:
  N1: U1.GPIO26, U1.GPIO27, U1.GPIO14, U1.GPIO12, DHT1.DATA, R1.Pin_0
  VIN: U1.GPIO10, U1.GPIO11, U1.VIN, DHT1.GND
  N2: U1.GPIO6, U1.GPIO7, DHT1.VDD, R1.Pin_1

custom parts:
  ESP32S-HiLetgo: HiLetgo ESP-WROOM-32 ESP32 ESP-32S Development Board 2.4GHz Dual-Mode WiFi + Bluetooth Dual Cores Microcontroller The ESP32 integrated with Antenna switches, RF Balun, power amplifiers, low-noise amplifiers, filters, and management modules, and the entire solution occupies the least area of PCB. 2.4 GHz Wi-Fi plus Bluetooth dual-mode chip, with TSMC Ultra-low power consumption 40nm technology,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
  DHT11 Humitidy and Temperature Sensor: DHT11 Humidity and Temperature Sensor
